// Digital circuit PDP8-X.dig as structural Verilog
module PDP8_X (
  input  clk
);

  wire A_out, AC2RAMD, AC_CK, add_1_c_o, add_2_c_o, AND, and_1_out, and_20_out, and_21_out, and_23_out,
       and_25_out, and_26_out, and_27_out, and_28_out, and_29_out, and_30_out, and_31_out, and_32_out,
       and_33_out, and_34_out, and_35_out, and_36_out, and_37_out, and_39_out, and_40_out, and_41_out,
       and_43_out, and_45_out, and_46_out, and_47_out, and_48_out, and_49_out, and_50_out, and_51_out,
       and_52_out, and_53_out, and_54_out, and_55_out, and_56_out, and_57_out, and_58_out, and_59_out,
       and_60_out, and_61_out, and_62_out, and_63_out, and_64_out, and_65_out, and_66_out, and_67_out,
       and_68_out, and_69_out, and_70_out, and_71_out, and_72_out, and_73_out, and_74_out, and_75_out,
       and_76_out, and_77_out, and_78_out, and_79_out, and_80_out, and_81_out, and_82_out, and_83_out,
       and_84_out, and_85_out, and_86_out, and_87_out, and_88_out, and_89_out, and_90_out, and_91_out,
       and_92_out, and_93_out, and_94_out, and_95_out, and_96_out, and_97_out, and_98_out, and_99_out,
       and_100_out, and_101_out, and_102_out, and_103_out, and_104_out, and_105_out, and_106_out,
       and_107_out, and_108_out, and_109_out, and_110_out, AUTOIND, CLA, CLAx, comparator_1_eq,
       counter_2_ovf, d_ff_1_q, DCA, demultiplexer_1_out_3, demultiplexer_1_out_7, demultiplexer_2_out_3,
       demultiplexer_2_out_7, demultiplexer_3_out_5, demultiplexer_3_out_6, demultiplexer_3_out_7,
       demultiplexer_3_out_8, demultiplexer_3_out_9, demultiplexer_3_out_10, demultiplexer_3_out_11,
       demultiplexer_3_out_12, demultiplexer_3_out_13, demultiplexer_3_out_14, demultiplexer_3_out_15,
       demultiplexer_3_out_16, demultiplexer_3_out_17, demultiplexer_3_out_18, demultiplexer_3_out_19,
       demultiplexer_3_out_20, demultiplexer_3_out_21, demultiplexer_3_out_22, demultiplexer_3_out_23,
       demultiplexer_3_out_24, demultiplexer_3_out_25, demultiplexer_3_out_26, demultiplexer_3_out_27,
       demultiplexer_3_out_28, demultiplexer_3_out_29, demultiplexer_3_out_30, demultiplexer_3_out_31,
       demultiplexer_3_out_32, demultiplexer_3_out_33, demultiplexer_3_out_34, demultiplexer_3_out_35,
       demultiplexer_3_out_36, demultiplexer_3_out_37, demultiplexer_3_out_38, demultiplexer_3_out_39,
       demultiplexer_3_out_40, demultiplexer_3_out_41, demultiplexer_3_out_42, demultiplexer_3_out_43,
       demultiplexer_3_out_44, demultiplexer_3_out_45, demultiplexer_3_out_46, demultiplexer_3_out_47,
       demultiplexer_3_out_48, demultiplexer_3_out_49, demultiplexer_3_out_50, demultiplexer_3_out_51,
       demultiplexer_3_out_52, demultiplexer_3_out_53, demultiplexer_3_out_54, demultiplexer_3_out_55,
       demultiplexer_3_out_56, demultiplexer_3_out_57, demultiplexer_3_out_58, demultiplexer_3_out_59,
       demultiplexer_3_out_60, demultiplexer_3_out_61, demultiplexer_3_out_62, demultiplexer_3_out_63,
       driver_27_out, driver_28_out, driver_56_out, driver_57_out, driver_58_out, driver_62_out,
       driver_63_out, driver_66_out, driver_67_out, driver_68_out, driver_95_out, driver_96_out,
       driver_124_out, driver_125_out, driver_126_out, driver_130_out, driver_131_out, driver_134_out,
       driver_135_out, driver_136_out, driver_159_out, driver_160_out, driver_161_out, driver_165_out,
       driver_166_out, driver_170_out, driver_171_out, driver_175_out, driver_176_out, driver_178_out,
       driver_179_out, driver_180_out, driver_181_out, driver_191_out, driver_201_out, driver_204_out,
       driver_205_out, driver_206_out, driver_209_out, driver_210_out, driver_211_out, driver_215_out,
       driver_216_out, driver_219_out, driver_220_out, driver_221_out, driver_224_out, driver_225_out,
       driver_226_out, driver_231_out, driver_235_out, driver_236_out, driver_240_out, driver_241_out,
       driver_246_out, driver_249_out, driver_250_out, driver_251_out, driver_255_out, driver_256_out,
       driver_259_out, driver_260_out, driver_261_out, driver_265_out, driver_266_out, driver_271_out,
       driver_274_out, driver_275_out, driver_276_out, driver_281_out, driver_285_out, driver_286_out,
       driver_287_out, driver_288_out, driver_289_out, driver_290_out, driver_291_out, driver_293_out,
       driver_294_out, driver_295_out, driver_300_out, driver_301_out, driver_306_out, driver_310_out,
       driver_311_out, driver_321_out, driver_324_out, driver_325_out, driver_326_out, driver_328_out,
       driver_329_out, driver_330_out, driver_334_out, driver_335_out, driver_336_out, driver_340_out,
       driver_341_out, driver_344_out, driver_345_out, driver_346_out, driver_348_out, driver_349_out,
       driver_350_out, driver_351_out, driver_355_out, driver_356_out, driver_360_out, driver_361_out,
       driver_369_out, driver_370_out, driver_371_out, driver_375_out, driver_376_out, driver_379_out,
       driver_380_out, driver_381_out, driver_385_out, driver_386_out, FLAG_PRNRDY, H_out, HALT, I_out,
       INC2RAMD, INCZERO, IND, IND2PC, IND2RAMA, IND_CK, INST_KCC, INST_KCF, INST_KIE, INST_KRB, INST_KRS,
       INST_KSF, INST_TCF, INST_TFL, INST_TLS, INST_TPC, INST_TSF, INST_TSK, IOT, IOT_DEVCPU, IOT_DEVHSP,
       IOT_DEVHSR, IOT_DEVKBD, IOT_DEVPRI, IR2PC, IR2RAMA, IR_CK, ISZ, JMP, JMS, LINK, LINK_CK,
       monoflop_1_nq, monoflop_1_q, monoflop_2_q, monoflop_3_q, monoflop_4_q, monoflop_5_q, NOIND, nor_2_out,
       NOTNOP, OPR, OPR1, OPR2, OPR_CLA1, OPR_CLA2, OPR_CLL, OPR_CMA, OPR_CML, OPR_HLT, OPR_IAC, OPR_LEFT,
       OPR_NA1, OPR_NOP, OPR_OSR, OPR_RIGHT, OPR_SMA, OPR_SNL, OPR_SZA, OPR_TSTINV, OPR_X2, or_1_out,
       or_3_out, or_4_out, or_5_out, or_6_out, or_7_out, or_8_out, or_9_out, or_10_out, or_12_out, or_13_out,
       PC2RAMA, PC2RAMD, PC_CK, PC_eq_200, PC_LD, PH00, PH01, PH02, PH03, PH04, PH05, PH06, PH07, PH08, PH09,
       PH10, PH11, PH12, PH13, PH14, PH15, R_out, RAM_OE, RAM_WE, RAMD2AC_ADD, RAMD2AC_AND, RAMD2IND,
       RAMD2PC, ROT2AC, rotater_1_p5, rs_ff_as_2_nq, rs_ff_as_2_q, rs_ff_as_3_q, rs_ff_as_4_q, S_out, SKIP,
       TAD, xor_1_out, xor_2_out;
  wire [2:0] DA0, DA1, DA2, DA3, IND0, IND1, IND2, IND3, RA0, RA1, RA2, RA3;
  wire [3:0] counter_3_out;
  wire [11:0] AC, add_1_s, add_2_s, and_38_out, and_42_out, and_44_out, bitextender_1_out, bitextender_2_out,
       bitextender_3_out, BUS_IR, BUS_PC, dipswitch_1_out, driver_89_out, INC_s, not_2_out, or_11_out, PCIN,
       RAMDATA, rotater_1_p4, xor_3_out;
  wire [14:0] counter_1_out;
  wire [31:0] AND_24_out, AND_i_auto_out, AND_i_out, COUNT_out, DCA_i_auto_out, DCA_i_out, DCA_out,
       INSTRUCTION_COUNT_out, ISZ_i_auto_out, ISZ_i_out, ISZ_out, JMP_i_auto_out, JMP_i_out, JMP_out,
       JMS_i_auto_out, JMS_i_out, JMS_out, OPR_GRP1_out, OPR_GRP2_out, TAD_i_auto_out, TAD_i_out, TAD_out;

  LED led_1 (.in(IOT));
  or or_1 (or_1_out, PH02, PH03, PH04, PH05, PH06, PH07, PH08, PH09, PH10, PH11);
  // Probe on BUS_IR[2:0]
  // Probe on BUS_IR[8:3]
  and and_1 (and_1_out, or_1_out, IOT);
  Demultiplexer #(.Selector_Bits(3)) demultiplexer_1 (
    .sel(BUS_IR[2:0]), .in(IOT_DEVKBD), .out_0(INST_KCF), .out_1(INST_KSF), .out_2(INST_KCC),
    .out_3(demultiplexer_1_out_3), .out_4(INST_KRS), .out_5(INST_KIE), .out_6(INST_KRB),
    .out_7(demultiplexer_1_out_7));
  LED led_2 (.in(IOT_DEVKBD));
  Demultiplexer #(.Selector_Bits(3)) demultiplexer_2 (
    .sel(BUS_IR[2:0]), .in(IOT_DEVPRI), .out_0(INST_TFL), .out_1(INST_TSF), .out_2(INST_TCF),
    .out_3(demultiplexer_2_out_3), .out_4(INST_TPC), .out_5(INST_TSK), .out_6(INST_TLS),
    .out_7(demultiplexer_2_out_7));
  LED led_3 (.in(IOT_DEVPRI));
  Demultiplexer #(.Selector_Bits(6)) demultiplexer_3 (
    .sel(BUS_IR[8:3]), .in(and_1_out), .out_0(IOT_DEVCPU), .out_1(IOT_DEVHSR), .out_2(IOT_DEVHSP),
    .out_3(IOT_DEVKBD), .out_4(IOT_DEVPRI), .out_5(demultiplexer_3_out_5), .out_6(demultiplexer_3_out_6),
    .out_7(demultiplexer_3_out_7), .out_8(demultiplexer_3_out_8), .out_9(demultiplexer_3_out_9),
    .out_10(demultiplexer_3_out_10), .out_11(demultiplexer_3_out_11), .out_12(demultiplexer_3_out_12),
    .out_13(demultiplexer_3_out_13), .out_14(demultiplexer_3_out_14), .out_15(demultiplexer_3_out_15),
    .out_16(demultiplexer_3_out_16), .out_17(demultiplexer_3_out_17), .out_18(demultiplexer_3_out_18),
    .out_19(demultiplexer_3_out_19), .out_20(demultiplexer_3_out_20), .out_21(demultiplexer_3_out_21),
    .out_22(demultiplexer_3_out_22), .out_23(demultiplexer_3_out_23), .out_24(demultiplexer_3_out_24),
    .out_25(demultiplexer_3_out_25), .out_26(demultiplexer_3_out_26), .out_27(demultiplexer_3_out_27),
    .out_28(demultiplexer_3_out_28), .out_29(demultiplexer_3_out_29), .out_30(demultiplexer_3_out_30),
    .out_31(demultiplexer_3_out_31), .out_32(demultiplexer_3_out_32), .out_33(demultiplexer_3_out_33),
    .out_34(demultiplexer_3_out_34), .out_35(demultiplexer_3_out_35), .out_36(demultiplexer_3_out_36),
    .out_37(demultiplexer_3_out_37), .out_38(demultiplexer_3_out_38), .out_39(demultiplexer_3_out_39),
    .out_40(demultiplexer_3_out_40), .out_41(demultiplexer_3_out_41), .out_42(demultiplexer_3_out_42),
    .out_43(demultiplexer_3_out_43), .out_44(demultiplexer_3_out_44), .out_45(demultiplexer_3_out_45),
    .out_46(demultiplexer_3_out_46), .out_47(demultiplexer_3_out_47), .out_48(demultiplexer_3_out_48),
    .out_49(demultiplexer_3_out_49), .out_50(demultiplexer_3_out_50), .out_51(demultiplexer_3_out_51),
    .out_52(demultiplexer_3_out_52), .out_53(demultiplexer_3_out_53), .out_54(demultiplexer_3_out_54),
    .out_55(demultiplexer_3_out_55), .out_56(demultiplexer_3_out_56), .out_57(demultiplexer_3_out_57),
    .out_58(demultiplexer_3_out_58), .out_59(demultiplexer_3_out_59), .out_60(demultiplexer_3_out_60),
    .out_61(demultiplexer_3_out_61), .out_62(demultiplexer_3_out_62), .out_63(demultiplexer_3_out_63));
  assign PC2RAMA = PH00 ? PH00 : 1'bz;  // Driver driver_1
  assign RAM_OE = PH00 ? PH00 : 1'bz;  // Driver driver_2
  assign PC2RAMA = PH01 ? PH01 : 1'bz;  // Driver driver_3
  assign RAM_OE = PH01 ? PH01 : 1'bz;  // Driver driver_4
  assign IR_CK = PH01 ? PH01 : 1'bz;  // Driver driver_5
  assign PC_CK = PH01 ? PH01 : 1'bz;  // Driver driver_6
  LED led_4 (.in(OPR));
  LED led_5 (.in(OPR1));
  LED led_6 (.in(OPR2));
  // Probe on BUS_IR
  Demultiplexer #(.Selector_Bits(3)) demultiplexer_4 (
    .sel(BUS_IR[11:9]), .in(1'b1), .out_0(AND), .out_1(TAD), .out_2(ISZ), .out_3(DCA), .out_4(JMS),
    .out_5(JMP), .out_6(IOT), .out_7(OPR));
  Demultiplexer demultiplexer_5 (.sel(BUS_IR[8]), .in(OPR), .out_0(OPR1), .out_1(OPR2));
  and and_2 (AUTOIND, BUS_IR[3], ~BUS_IR[4], ~BUS_IR[5], ~BUS_IR[6], ~BUS_IR[7], BUS_IR[8]);  // And
  not not_1 (NOIND, BUS_IR[8]);
  LED led_7 (.in(AUTOIND));
  nor nor_1 (IND, AUTOIND, NOIND);
  LED led_8 (.in(IND));
  and and_3 (OPR_IAC, BUS_IR[0], OPR1);
  LED led_9 (.in(OPR_IAC));
  and and_4 (OPR_X2, BUS_IR[1], OPR1);
  LED led_10 (.in(OPR_X2));
  and and_5 (OPR_LEFT, BUS_IR[2], OPR1);
  LED led_11 (.in(OPR_LEFT));
  and and_6 (OPR_RIGHT, BUS_IR[3], OPR1);
  LED led_12 (.in(OPR_RIGHT));
  and and_7 (OPR_CML, BUS_IR[4], OPR1);
  LED led_13 (.in(OPR_CML));
  and and_8 (OPR_CMA, BUS_IR[5], OPR1);
  LED led_14 (.in(OPR_CMA));
  and and_9 (OPR_CLL, BUS_IR[6], OPR1);
  LED led_15 (.in(OPR_CLL));
  and and_10 (OPR_CLA1, BUS_IR[7], OPR1);
  LED led_16 (.in(OPR_CLA1));
  and and_11 (OPR_NA1, BUS_IR[0], OPR2);
  LED led_17 (.in(OPR_NA1));
  and and_12 (OPR_HLT, BUS_IR[1], OPR2);
  LED led_18 (.in(OPR_HLT));
  and and_13 (OPR_OSR, BUS_IR[2], OPR2);
  LED led_19 (.in(OPR_OSR));
  and and_14 (OPR_TSTINV, BUS_IR[3], OPR2);
  LED led_20 (.in(OPR_TSTINV));
  and and_15 (OPR_SNL, BUS_IR[4], OPR2);
  LED led_21 (.in(OPR_SNL));
  and and_16 (OPR_SZA, BUS_IR[5], OPR2);
  LED led_22 (.in(OPR_SZA));
  and and_17 (OPR_SMA, BUS_IR[6], OPR2);
  LED led_23 (.in(OPR_SMA));
  and and_18 (OPR_CLA2, BUS_IR[7], OPR2);
  LED led_24 (.in(OPR_CLA2));
  or or_2 (NOTNOP, BUS_IR[0], BUS_IR[1], BUS_IR[2], BUS_IR[3], BUS_IR[4], BUS_IR[5], BUS_IR[6], BUS_IR[7]);
  and and_19 (OPR_NOP, NOTNOP, OPR);
  LED led_25 (.in(OPR_NOP));
  PullDown pulldown_1 (.out(PC_LD));
  PullDown pulldown_2 (.out(IR2PC));
  PullDown pulldown_3 (.out(IR2PC));
  PullDown pulldown_4 (.out(IND_CK));
  PullDown pulldown_5 (.out(IND2PC));
  PullDown pulldown_6 (.out(IR2RAMA));
  PullDown pulldown_7 (.out(IR2RAMA));
  PullDown pulldown_8 (.out(AC_CK));
  PullDown pulldown_9 (.out(LINK_CK));
  PullDown pulldown_10 (.out(RAMD2PC));
  PullDown pulldown_11 (.out(IND2RAMA));
  PullDown pulldown_12 (.out(INC2RAMD));
  PullDown pulldown_13 (.out(IR_CK));
  PullDown pulldown_14 (.out(RAM_WE));
  PullDown pulldown_15 (.out(PC_CK));
  PullDown pulldown_16 (.out(PC2RAMD));
  PullDown pulldown_17 (.out(ROT2AC));
  PullDown pulldown_18 (.out(RAMD2AC_ADD));
  PullDown pulldown_19 (.out(RAM_OE));
  Seven_Seg_Hex seven_seg_hex_1 (.d({1'b0, BUS_PC[11:9]}), .dp(1'b0));
  Seven_Seg_Hex seven_seg_hex_2 (.d({1'b0, BUS_IR[11:9]}), .dp(1'b0));
  Seven_Seg_Hex seven_seg_hex_3 (.d({1'b0, AC[11:9]}), .dp(1'b0));
  Seven_Seg_Hex seven_seg_hex_4 (.d({1'b0, IND3}), .dp(1'b0));
  Seven_Seg_Hex seven_seg_hex_5 (.d({1'b0, RA3}), .dp(1'b0));
  Seven_Seg_Hex seven_seg_hex_6 (.d({1'b0, RAMDATA[11:9]}), .dp(1'b0));
  Seven_Seg_Hex seven_seg_hex_7 (.d({1'b0, PCIN[11:9]}), .dp(1'b0));
  Seven_Seg_Hex seven_seg_hex_8 (.d({1'b0, DA3}), .dp(1'b0));
  or or_3 (or_3_out, INST_TPC, INST_TLS);
  Seven_Seg_Hex seven_seg_hex_9 (.d({1'b0, BUS_PC[8:6]}), .dp(1'b0));
  Seven_Seg_Hex seven_seg_hex_10 (.d({1'b0, BUS_IR[8:6]}), .dp(1'b0));
  Seven_Seg_Hex seven_seg_hex_11 (.d({1'b0, AC[8:6]}), .dp(1'b0));
  Seven_Seg_Hex seven_seg_hex_12 (.d({1'b0, IND2}), .dp(1'b0));
  Seven_Seg_Hex seven_seg_hex_13 (.d({1'b0, RA2}), .dp(1'b0));
  Seven_Seg_Hex seven_seg_hex_14 (.d({1'b0, RAMDATA[8:6]}), .dp(1'b0));
  Seven_Seg_Hex seven_seg_hex_15 (.d({1'b0, PCIN[8:6]}), .dp(1'b0));
  Seven_Seg_Hex seven_seg_hex_16 (.d({1'b0, DA2}), .dp(1'b0));
  Seven_Seg_Hex seven_seg_hex_17 (.d({1'b0, BUS_PC[5:3]}), .dp(1'b0));
  Seven_Seg_Hex seven_seg_hex_18 (.d({1'b0, BUS_IR[5:3]}), .dp(1'b0));
  Seven_Seg_Hex seven_seg_hex_19 (.d({1'b0, AC[5:3]}), .dp(1'b0));
  Seven_Seg_Hex seven_seg_hex_20 (.d({1'b0, IND1}), .dp(1'b0));
  Seven_Seg_Hex seven_seg_hex_21 (.d({1'b0, RA1}), .dp(1'b0));
  Seven_Seg_Hex seven_seg_hex_22 (.d({1'b0, RAMDATA[5:3]}), .dp(1'b0));
  Seven_Seg_Hex seven_seg_hex_23 (.d({1'b0, PCIN[5:3]}), .dp(1'b0));
  Seven_Seg_Hex seven_seg_hex_24 (.d({1'b0, DA1}), .dp(1'b0));
  Counter #(.Bits(32)) INSTRUCTION_COUNT (.en(1'b1), .C(PH01), .clr(1'b0), .out(INSTRUCTION_COUNT_out));  // open: ovf
  Monoflop #(.timerDelay(300)) monoflop_1 (.C(or_3_out), .R(1'b0), .Q(monoflop_1_q), .nQ(monoflop_1_nq));
  Seven_Seg_Hex seven_seg_hex_25 (.d({1'b0, BUS_PC[2:0]}), .dp(1'b0));
  Seven_Seg_Hex seven_seg_hex_26 (.d({1'b0, BUS_IR[2:0]}), .dp(1'b0));
  Seven_Seg_Hex seven_seg_hex_27 (.d({1'b0, AC[2:0]}), .dp(1'b0));
  Seven_Seg_Hex seven_seg_hex_28 (.d({1'b0, IND0}), .dp(1'b0));
  Seven_Seg_Hex seven_seg_hex_29 (.d({1'b0, RA0}), .dp(1'b0));
  Seven_Seg_Hex seven_seg_hex_30 (.d({1'b0, RAMDATA[2:0]}), .dp(1'b0));
  Seven_Seg_Hex seven_seg_hex_31 (.d({1'b0, PCIN[2:0]}), .dp(1'b0));
  Seven_Seg_Hex seven_seg_hex_32 (.d({1'b0, DA0}), .dp(1'b0));
  // Probe on INSTRUCTION_COUNT_out
  Counter #(.Bits(32)) COUNT (.en(1'b1), .C(or_3_out), .clr(1'b0), .out(COUNT_out));  // open: ovf
  Terminal #(.termWidth(20), .termHeight(10)) PRN (.D(AC[7:0]), .C(or_3_out), .en(1'b1));
  // Probe on COUNT_out
  LED led_26 (.in(INST_KCF));
  LED led_27 (.in(OPR_CLA1));
  LED led_28 (.in(AND));
  LED led_29 (.in(LINK));
  Monoflop monoflop_2 (.C(monoflop_1_q), .R(1'b0), .Q(monoflop_2_q));  // open: nQ
  Monoflop monoflop_3 (.C(monoflop_1_nq), .R(1'b0), .Q(monoflop_3_q));  // open: nQ
  LED led_30 (.in(INST_KSF));
  LED led_31 (.in(OPR_CLL));
  LED led_32 (.in(TAD));
  or or_4 (or_4_out, INST_TFL, monoflop_2_q);
  or or_5 (or_5_out, monoflop_3_q, INST_TCF);
  LED led_33 (.in(INST_KCC));
  LED led_34 (.in(INST_KRS));
  LED led_35 (.in(OPR_CMA));
  LED led_36 (.in(OPR_CML));
  LED led_37 (.in(ISZ));
  LED led_38 (.in(DCA));
  RS_FF_AS rs_ff_as_1 (.S(or_4_out), .R(or_5_out), .nQ(FLAG_PRNRDY));  // open: Q
  LED led_39 (.in(IR2PC));
  LED led_40 (.in(IR2RAMA));
  assign PC_CK = PC_eq_200 ? PC_eq_200 : 1'bz;  // Driver driver_7
  assign PC_LD = PC_eq_200 ? PC_eq_200 : 1'bz;  // Driver driver_8
  LED led_41 (.in(INST_KIE));
  LED led_42 (.in(OPR_IAC));
  LED led_43 (.in(JMS));
  // OC12 oc12_1: pin names not known; wires that end beside it: BUS_IR[6:0], BUS_PC[11:7], BUS_IR[7], IR2PC, PCIN[6:0], PCIN[11:7], PCIN
  // OC12 oc12_2: pin names not known; wires that end beside it: BUS_IR[6:0], BUS_PC[11:7], BUS_IR[7], IR2RAMA, {RA2[0], RA1, RA0}, {RA3, RA2[2:1]}
  assign PCIN = PC_eq_200 ? 12'h80 : 12'bz;  // Driver driver_9
  LED led_44 (.in(INST_KRB));
  LED led_45 (.in(OPR_RIGHT));
  LED led_46 (.in(JMP));
  Button S (.out(S_out));
  Button I (.out(I_out));
  Button R (.out(R_out));
  Button H (.out(H_out));
  Button A (.out(A_out));
  Button _2 (.out(PC_eq_200));
  LED led_47 (.in(INST_TFL));
  LED led_48 (.in(OPR_LEFT));
  LED led_49 (.in(OPR_X2));
  LED led_50 (.in(IOT));
  LED led_51 (.in(OPR));
  or or_6 (or_6_out, I_out, and_20_out);
  LED led_52 (.in(and_20_out));
  Monoflop #(.timerDelay(2)) monoflop_4 (.C(A_out), .R(1'b0), .Q(monoflop_4_q));  // open: nQ
  // Probe on PCIN
  LED led_53 (.in(PC_CK));
  LED led_54 (.in(PC_LD));
  LED led_55 (.in(RAMD2PC));
  assign PCIN = RAMD2PC ? {DA3, DA2, DA1, DA0} : 12'bz;  // Driver driver_10
  LED led_56 (.in(IND2PC));
  assign PCIN = IND2PC ? {IND3, IND2, IND1, IND0} : 12'bz;  // Driver driver_11
  LED led_57 (.in(INST_TSF));
  LED led_58 (.in(OPR_CLA2));
  LED led_59 (.in(or_6_out));
  and and_20 (and_20_out, rs_ff_as_2_q, counter_2_ovf);
  RS_FF_AS rs_ff_as_2 (.S(monoflop_4_q), .R(comparator_1_eq), .Q(rs_ff_as_2_q), .nQ(rs_ff_as_2_nq));
  CounterPreset #(.Bits(12)) PC (
    .en(1'b1), .C(PC_CK), .dir(1'b0), .in(PCIN), .ld(PC_LD), .clr(1'b0), .out(BUS_PC));  // open: ovf
  LED led_60 (.in(INST_TCF));
  LED led_61 (.in(OPR_SMA));
  LED led_62 (.in(NOIND));
  LED led_63 (.in(IND));
  Monoflop #(.timerDelay(2)) monoflop_5 (.C(or_6_out), .R(1'b0), .Q(monoflop_5_q));  // open: nQ
  RS_FF_AS rs_ff_as_3 (.S(R_out), .R(or_7_out), .Q(rs_ff_as_3_q));  // open: nQ
  or or_7 (or_7_out, H_out, HALT);
  LED led_64 (.in(or_7_out));
  LED led_65 (.in(INST_TPC));
  LED led_66 (.in(INST_TSK));
  LED led_67 (.in(OPR_SZA));
  LED led_68 (.in(OPR_SNL));
  LED led_69 (.in(AUTOIND));
  or or_8 (or_8_out, monoflop_5_q, R_out, rs_ff_as_3_q);
  Counter #(.Bits(15)) counter_1 (
    .en(rs_ff_as_2_q), .C(counter_2_ovf), .clr(rs_ff_as_2_nq), .out(counter_1_out));  // open: ovf
  // Probe on BUS_PC
  LED led_70 (.in(INST_TLS));
  LED led_71 (.in(OPR_TSTINV));
  LED led_72 (.in(BUS_IR[7]));
  LED led_73 (.in(or_8_out));
  Comparator #(.Bits(15)) comparator_1 (.a(counter_1_out), .b(15'h29), .eq(comparator_1_eq));  // open: gt, lt
  and and_21 (and_21_out, INST_TSF, FLAG_PRNRDY, PH04);
  and and_22 (HALT, OPR_HLT, PH02);
  LED led_74 (.in(OPR_OSR));
  D_FF d_ff_1 (.D(PH10), .C(clk), .Q(d_ff_1_q));  // open: nQ
  LED led_75 (.in(and_21_out));
  LED led_76 (.in(HALT));
  LED led_77 (.in(PC2RAMA));
  assign {RA3, RA2, RA1, RA0} = PC2RAMA ? BUS_PC : 12'bz;  // Driver driver_12
  LED led_78 (.in(OPR_HLT));
  LED led_79 (.in(OPR_NA1));
  Counter #(.Bits(4)) counter_2 (.en(1'b1), .C(clk), .clr(1'b0), .ovf(counter_2_ovf));  // open: out
  assign IR_CK = and_21_out ? and_21_out : 1'bz;  // Driver driver_13
  assign PC_CK = and_21_out ? and_21_out : 1'bz;  // Driver driver_14
  Driver driver_15 (.in(and_21_out), .en(and_21_out));  // open: out
  Driver driver_16 (.in(and_21_out), .en(and_21_out));  // open: out
  Driver driver_17 (.in(and_21_out), .en(and_21_out));  // open: out
  // Probe on {RA3, RA2, RA1, RA0}
  LED led_80 (.in(IND2RAMA));
  LED led_81 (.in(OPR_NOP));
  RS_FF_AS rs_ff_as_4 (.S(or_8_out), .R(d_ff_1_q), .Q(rs_ff_as_4_q));  // open: nQ
  LED led_82 (.in(RAM_WE));
  LED led_83 (.in(RAM_OE));
  assign {RA3, RA2, RA1, RA0} = IND2RAMA ? {IND3, IND2, IND1, IND0} : 12'bz;  // Driver driver_18
  and and_23 (and_23_out, clk, rs_ff_as_4_q);
  EEPROM #(.AddrBits(12), .isProgramMemory("true"), .Bits(12)) eeprom_1 (
    .A({RA3, RA2, RA1, RA0}), .CS(1'b1), .WE(RAM_WE), .OE(RAM_OE), .D(RAMDATA));
  or or_9 (or_9_out, S_out, and_23_out);
  LED led_84 (.in(and_23_out));
  Counter #(.Bits(4)) counter_3 (.en(1'b1), .C(or_9_out), .clr(PH10), .out(counter_3_out));  // open: ovf
  LED led_85 (.in(or_9_out));
  // Probe on RAMDATA
  Seven_Seg_Hex seven_seg_hex_33 (.d(counter_3_out), .dp(1'b0));
  Decoder #(.Selector_Bits(4)) decoder_1 (
    .sel(counter_3_out), .out_0(PH00), .out_1(PH01), .out_2(PH02), .out_3(PH03), .out_4(PH04), .out_5(PH05),
    .out_6(PH06), .out_7(PH07), .out_8(PH08), .out_9(PH09), .out_10(PH10), .out_11(PH11), .out_12(PH12),
    .out_13(PH13), .out_14(PH14), .out_15(PH15));
  assign {DA3, DA2, DA1, DA0} = RAM_OE ? RAMDATA : 12'bz;  // Driver driver_19
  assign RAMDATA = RAM_WE ? {DA3, DA2, DA1, DA0} : 12'bz;  // Driver driver_20
  LED led_86 (.in(PC2RAMD));
  // Probe on {DA3, DA2, DA1, DA0}
  assign {DA3, DA2, DA1, DA0} = PC2RAMD ? BUS_PC : 12'bz;  // Driver driver_21
  D_FF #(.Bits(12)) IR (.D({DA3, DA2, DA1, DA0}), .C(IR_CK), .Q(BUS_IR));  // open: nQ
  LED led_87 (.in(IR_CK));
  LED led_88 (.in(INC2RAMD));
  assign {DA3, DA2, DA1, DA0} = INC2RAMD ? INC_s : 12'bz;  // Driver driver_22
  LED led_89 (.in(AC2RAMD));
  assign {DA3, DA2, DA1, DA0} = AC2RAMD ? AC : 12'bz;  // Driver driver_23
  // Probe on BUS_IR
  Counter #(.Bits(32)) AND_24 (.en(1'b1), .C(and_25_out), .clr(1'b0), .out(AND_24_out));  // open: ovf
  and and_25 (and_25_out, AND, NOIND, PH02);
  and and_26 (and_26_out, AND, NOIND, PH03);
  D_FF #(.Bits(12)) u_IND (.D({DA3, DA2, DA1, DA0}), .C(IND_CK), .Q({IND3, IND2, IND1, IND0}));  // open: nQ
  LED led_90 (.in(IND_CK));
  // Probe on AND_24_out
  LED led_91 (.in(and_25_out));
  LED led_92 (.in(and_26_out));
  assign IR2RAMA = and_25_out ? and_25_out : 1'bz;  // Driver driver_24
  assign RAMD2AC_AND = and_25_out ? and_25_out : 1'bz;  // Driver driver_25
  assign RAM_OE = and_25_out ? and_25_out : 1'bz;  // Driver driver_26
  assign driver_27_out = and_25_out ? and_25_out : 1'bz;  // Driver driver_27
  assign driver_28_out = and_25_out ? and_25_out : 1'bz;  // Driver driver_28
  assign IR2RAMA = and_26_out ? and_26_out : 1'bz;  // Driver driver_29
  assign RAMD2AC_AND = and_26_out ? and_26_out : 1'bz;  // Driver driver_30
  assign RAM_OE = and_26_out ? and_26_out : 1'bz;  // Driver driver_31
  assign AC_CK = and_26_out ? and_26_out : 1'bz;  // Driver driver_32
  Driver driver_33 (.in(and_26_out), .en(and_26_out));  // open: out
  // Probe on {IND3, IND2, IND1, IND0}
  Add #(.Bits(12)) INC (.a({12{1'b0}}), .b({IND3, IND2, IND1, IND0}), .c_i(1'b1), .s(INC_s), .c_o(INCZERO));
  Counter #(.Bits(32)) AND_i (.en(1'b1), .C(and_27_out), .clr(1'b0), .out(AND_i_out));  // open: ovf
  and and_27 (and_27_out, AND, IND, PH02);
  LED led_93 (.in(and_27_out));
  and and_28 (and_28_out, AND, IND, PH03);
  LED led_94 (.in(and_28_out));
  and and_29 (and_29_out, AND, IND, PH04);
  LED led_95 (.in(and_29_out));
  and and_30 (and_30_out, AND, IND, PH05);
  LED led_96 (.in(and_30_out));
  // Probe on AND_i_out
  assign IR2RAMA = and_27_out ? and_27_out : 1'bz;  // Driver driver_34
  assign RAMD2IND = and_27_out ? and_27_out : 1'bz;  // Driver driver_35
  assign RAM_OE = and_27_out ? and_27_out : 1'bz;  // Driver driver_36
  Driver driver_37 (.in(and_27_out), .en(and_27_out));  // open: out
  Driver driver_38 (.in(and_27_out), .en(and_27_out));  // open: out
  assign IR2RAMA = and_28_out ? and_28_out : 1'bz;  // Driver driver_39
  assign RAMD2IND = and_28_out ? and_28_out : 1'bz;  // Driver driver_40
  assign RAM_OE = and_28_out ? and_28_out : 1'bz;  // Driver driver_41
  assign IND_CK = and_28_out ? and_28_out : 1'bz;  // Driver driver_42
  Driver driver_43 (.in(and_28_out), .en(and_28_out));  // open: out
  assign IND2RAMA = and_29_out ? and_29_out : 1'bz;  // Driver driver_44
  assign RAMD2AC_AND = and_29_out ? and_29_out : 1'bz;  // Driver driver_45
  assign RAM_OE = and_29_out ? and_29_out : 1'bz;  // Driver driver_46
  Driver driver_47 (.in(and_29_out), .en(and_29_out));  // open: out
  Driver driver_48 (.in(and_29_out), .en(and_29_out));  // open: out
  assign IND2RAMA = and_30_out ? and_30_out : 1'bz;  // Driver driver_49
  assign RAMD2AC_AND = and_30_out ? and_30_out : 1'bz;  // Driver driver_50
  assign RAM_OE = and_30_out ? and_30_out : 1'bz;  // Driver driver_51
  assign AC_CK = and_30_out ? and_30_out : 1'bz;  // Driver driver_52
  Driver driver_53 (.in(and_30_out), .en(and_30_out));  // open: out
  Counter #(.Bits(32)) AND_i_auto (.en(1'b1), .C(and_31_out), .clr(1'b0), .out(AND_i_auto_out));  // open: ovf
  and and_31 (and_31_out, AND, AUTOIND, PH02);
  and and_32 (and_32_out, AND, AUTOIND, PH03);
  and and_33 (and_33_out, AND, AUTOIND, PH04);
  and and_34 (and_34_out, AND, IND, PH05);
  and and_35 (and_35_out, AND, IND, PH06);
  and and_36 (and_36_out, AND, IND, PH07);
  and and_37 (and_37_out, AND, IND, PH08);
  Add #(.Bits(12)) add_1 (.a(AC), .b({DA3, DA2, DA1, DA0}), .c_i(1'b0), .s(add_1_s), .c_o(add_1_c_o));
  assign and_38_out = AC & {DA3, DA2, DA1, DA0};  // And and_38, 12 bits wide
  // Probe on AND_i_auto_out
  LED led_97 (.in(and_31_out));
  LED led_98 (.in(and_32_out));
  LED led_99 (.in(and_33_out));
  LED led_100 (.in(and_34_out));
  LED led_101 (.in(and_35_out));
  LED led_102 (.in(and_36_out));
  LED led_103 (.in(and_37_out));
  assign IR2RAMA = and_31_out ? and_31_out : 1'bz;  // Driver driver_54
  assign RAM_OE = and_31_out ? and_31_out : 1'bz;  // Driver driver_55
  assign driver_56_out = and_31_out ? and_31_out : 1'bz;  // Driver driver_56
  assign driver_57_out = and_31_out ? and_31_out : 1'bz;  // Driver driver_57
  assign driver_58_out = and_31_out ? and_31_out : 1'bz;  // Driver driver_58
  assign IR2RAMA = and_32_out ? and_32_out : 1'bz;  // Driver driver_59
  assign IND_CK = and_32_out ? and_32_out : 1'bz;  // Driver driver_60
  assign RAM_OE = and_32_out ? and_32_out : 1'bz;  // Driver driver_61
  assign driver_62_out = and_32_out ? and_32_out : 1'bz;  // Driver driver_62
  assign driver_63_out = and_32_out ? and_32_out : 1'bz;  // Driver driver_63
  assign INC2RAMD = and_33_out ? and_33_out : 1'bz;  // Driver driver_64
  assign RAM_WE = and_33_out ? and_33_out : 1'bz;  // Driver driver_65
  assign driver_66_out = and_33_out ? and_33_out : 1'bz;  // Driver driver_66
  assign driver_67_out = and_33_out ? and_33_out : 1'bz;  // Driver driver_67
  assign driver_68_out = and_33_out ? and_33_out : 1'bz;  // Driver driver_68
  assign IR2RAMA = and_34_out ? and_34_out : 1'bz;  // Driver driver_69
  assign RAMD2IND = and_34_out ? and_34_out : 1'bz;  // Driver driver_70
  assign RAM_OE = and_34_out ? and_34_out : 1'bz;  // Driver driver_71
  Driver driver_72 (.in(and_34_out), .en(and_34_out));  // open: out
  Driver driver_73 (.in(and_34_out), .en(and_34_out));  // open: out
  assign IR2RAMA = and_35_out ? and_35_out : 1'bz;  // Driver driver_74
  assign RAMD2IND = and_35_out ? and_35_out : 1'bz;  // Driver driver_75
  assign RAM_OE = and_35_out ? and_35_out : 1'bz;  // Driver driver_76
  assign IND_CK = and_35_out ? and_35_out : 1'bz;  // Driver driver_77
  Driver driver_78 (.in(and_35_out), .en(and_35_out));  // open: out
  assign IND2RAMA = and_36_out ? and_36_out : 1'bz;  // Driver driver_79
  assign RAMD2AC_AND = and_36_out ? and_36_out : 1'bz;  // Driver driver_80
  assign RAM_OE = and_36_out ? and_36_out : 1'bz;  // Driver driver_81
  Driver driver_82 (.in(and_36_out), .en(and_36_out));  // open: out
  Driver driver_83 (.in(and_36_out), .en(and_36_out));  // open: out
  assign IND2RAMA = and_37_out ? and_37_out : 1'bz;  // Driver driver_84
  assign RAMD2AC_AND = and_37_out ? and_37_out : 1'bz;  // Driver driver_85
  assign RAM_OE = and_37_out ? and_37_out : 1'bz;  // Driver driver_86
  assign AC_CK = and_37_out ? and_37_out : 1'bz;  // Driver driver_87
  Driver driver_88 (.in(and_37_out), .en(and_37_out));  // open: out
  // Probe on AC
  // Probe on add_1_s
  // Probe on and_38_out
  // Probe on rotater_1_p4
  and and_39 (and_39_out, add_1_c_o, RAMD2AC_ADD);
  xor xor_1 (xor_1_out, and_39_out, rotater_1_p5);
  assign driver_89_out = RAMD2AC_ADD ? add_1_s : 12'bz;  // Driver driver_89
  LED led_104 (.in(RAMD2AC_ADD));
  assign driver_89_out = RAMD2AC_AND ? and_38_out : 12'bz;  // Driver driver_90
  LED led_105 (.in(RAMD2AC_AND));
  assign driver_89_out = ROT2AC ? rotater_1_p4 : 12'bz;  // Driver driver_91
  LED led_106 (.in(ROT2AC));
  // Probe on driver_89_out
  D_FF u_LINK (.D(xor_1_out), .C(LINK_CK), .Q(LINK));  // open: nQ
  LED led_107 (.in(LINK_CK));
  Counter #(.Bits(32)) u_TAD (.en(1'b1), .C(and_40_out), .clr(1'b0), .out(TAD_out));  // open: ovf
  and and_40 (and_40_out, TAD, NOIND, PH02);
  LED led_108 (.in(and_40_out));
  D_FF #(.Bits(12)) u_AC (.D(driver_89_out), .C(AC_CK), .Q(AC));  // open: nQ
  LED led_109 (.in(AC_CK));
  // Probe on TAD_out
  assign IR2RAMA = and_40_out ? and_40_out : 1'bz;  // Driver driver_92
  assign RAMD2AC_ADD = and_40_out ? and_40_out : 1'bz;  // Driver driver_93
  assign RAM_OE = and_40_out ? and_40_out : 1'bz;  // Driver driver_94
  assign driver_95_out = and_40_out ? and_40_out : 1'bz;  // Driver driver_95
  assign driver_96_out = and_40_out ? and_40_out : 1'bz;  // Driver driver_96
  // Probe on AC
  or or_10 (or_10_out, OPR_CLA2, OPR_CLA1, CLAx);
  and and_41 (and_41_out, TAD, NOIND, PH03);
  BitExtender #(.inputBits(1), .outputBits(12)) bitextender_1 (.in(or_10_out), .out(bitextender_1_out));
  LED led_110 (.in(or_10_out));
  assign IR2RAMA = and_41_out ? and_41_out : 1'bz;  // Driver driver_97
  LED led_111 (.in(and_41_out));
  assign RAMD2AC_ADD = and_41_out ? and_41_out : 1'bz;  // Driver driver_98
  assign RAM_OE = and_41_out ? and_41_out : 1'bz;  // Driver driver_99
  assign AC_CK = and_41_out ? and_41_out : 1'bz;  // Driver driver_100
  assign LINK_CK = and_41_out ? and_41_out : 1'bz;  // Driver driver_101
  assign and_42_out = AC & ~bitextender_1_out;  // And and_42, 12 bits wide
  and and_43 (and_43_out, LINK, ~OPR_CLL);  // And
  DipSwitch #(.dipDefault("true")) dipswitch_1 (.out(dipswitch_1_out[11]));
  DipSwitch #(.dipDefault("true")) dipswitch_2 (.out(dipswitch_1_out[10]));
  DipSwitch #(.dipDefault("true")) dipswitch_3 (.out(dipswitch_1_out[9]));
  assign or_11_out = and_44_out | and_42_out;  // Or or_11, 12 bits wide
  LED led_112 (.in(and_43_out));
  DipSwitch dipswitch_4 (.out(dipswitch_1_out[8]));
  DipSwitch dipswitch_5 (.out(dipswitch_1_out[7]));
  DipSwitch dipswitch_6 (.out(dipswitch_1_out[6]));
  BitExtender #(.inputBits(1), .outputBits(12)) bitextender_2 (.in(OPR_CMA), .out(bitextender_2_out));
  xor xor_2 (xor_2_out, and_43_out, OPR_CML);
  DipSwitch dipswitch_7 (.out(dipswitch_1_out[5]));
  DipSwitch dipswitch_8 (.out(dipswitch_1_out[4]));
  DipSwitch dipswitch_9 (.out(dipswitch_1_out[3]));
  assign and_44_out = bitextender_3_out & not_2_out;  // And and_44, 12 bits wide
  assign xor_3_out = or_11_out ^ bitextender_2_out;  // XOr xor_3, 12 bits wide
  LED led_113 (.in(xor_2_out));
  Counter #(.Bits(32)) TAD_i (.en(1'b1), .C(and_45_out), .clr(1'b0), .out(TAD_i_out));  // open: ovf
  and and_45 (and_45_out, TAD, IND, PH02);
  and and_46 (and_46_out, TAD, IND, PH03);
  LED led_114 (.in(and_46_out));
  and and_47 (and_47_out, TAD, IND, PH04);
  LED led_115 (.in(and_47_out));
  and and_48 (and_48_out, TAD, IND, PH05);
  LED led_116 (.in(and_48_out));
  DipSwitch #(.dipDefault("true")) dipswitch_10 (.out(dipswitch_1_out[2]));
  DipSwitch #(.dipDefault("true")) dipswitch_11 (.out(dipswitch_1_out[1]));
  DipSwitch #(.dipDefault("true")) dipswitch_12 (.out(dipswitch_1_out[0]));
  assign not_2_out = ~dipswitch_1_out;  // Not not_2, 12 bits wide
  // Probe on not_2_out
  BitExtender #(.inputBits(1), .outputBits(12)) bitextender_3 (.in(OPR_OSR), .out(bitextender_3_out));
  // Probe on TAD_i_out
  assign IR2RAMA = and_45_out ? and_45_out : 1'bz;  // Driver driver_102
  LED led_117 (.in(and_45_out));
  assign RAMD2IND = and_45_out ? and_45_out : 1'bz;  // Driver driver_103
  assign RAM_OE = and_45_out ? and_45_out : 1'bz;  // Driver driver_104
  Driver driver_105 (.in(and_45_out), .en(and_45_out));  // open: out
  Driver driver_106 (.in(and_45_out), .en(and_45_out));  // open: out
  assign IR2RAMA = and_46_out ? and_46_out : 1'bz;  // Driver driver_107
  assign RAMD2IND = and_46_out ? and_46_out : 1'bz;  // Driver driver_108
  assign RAM_OE = and_46_out ? and_46_out : 1'bz;  // Driver driver_109
  assign IND_CK = and_46_out ? and_46_out : 1'bz;  // Driver driver_110
  Driver driver_111 (.in(and_46_out), .en(and_46_out));  // open: out
  assign IND2RAMA = and_47_out ? and_47_out : 1'bz;  // Driver driver_112
  assign RAMD2AC_ADD = and_47_out ? and_47_out : 1'bz;  // Driver driver_113
  assign RAM_OE = and_47_out ? and_47_out : 1'bz;  // Driver driver_114
  Driver driver_115 (.in(and_47_out), .en(and_47_out));  // open: out
  Driver driver_116 (.in(and_47_out), .en(and_47_out));  // open: out
  assign IND2RAMA = and_48_out ? and_48_out : 1'bz;  // Driver driver_117
  assign RAMD2AC_ADD = and_48_out ? and_48_out : 1'bz;  // Driver driver_118
  assign RAM_OE = and_48_out ? and_48_out : 1'bz;  // Driver driver_119
  assign AC_CK = and_48_out ? and_48_out : 1'bz;  // Driver driver_120
  assign LINK_CK = and_48_out ? and_48_out : 1'bz;  // Driver driver_121
  Add #(.Bits(12)) add_2 (.a(xor_3_out), .b({12{1'b0}}), .c_i(OPR_IAC), .s(add_2_s), .c_o(add_2_c_o));
  or or_12 (or_12_out, add_2_c_o, xor_2_out);
  LED led_118 (.in(or_12_out));
  // ROTATER rotater_1: pin names not known; wires that end beside it: {OPR_RIGHT, OPR_LEFT, OPR_X2}, add_2_s, or_12_out, rotater_1_p4, rotater_1_p5
  Counter #(.Bits(32)) TAD_i_auto (.en(1'b1), .C(and_49_out), .clr(1'b0), .out(TAD_i_auto_out));  // open: ovf
  and and_49 (and_49_out, TAD, AUTOIND, PH02);
  and and_50 (and_50_out, TAD, AUTOIND, PH03);
  and and_51 (and_51_out, TAD, AUTOIND, PH04);
  and and_52 (and_52_out, TAD, AUTOIND, PH05);
  and and_53 (and_53_out, TAD, AUTOIND, PH06);
  and and_54 (and_54_out, TAD, AUTOIND, PH07);
  and and_55 (and_55_out, TAD, AUTOIND, PH08);
  // Probe on rotater_1_p4
  // Probe on TAD_i_auto_out
  LED led_119 (.in(and_49_out));
  LED led_120 (.in(and_50_out));
  LED led_121 (.in(and_51_out));
  LED led_122 (.in(and_52_out));
  LED led_123 (.in(and_53_out));
  LED led_124 (.in(and_54_out));
  LED led_125 (.in(and_55_out));
  assign IR2RAMA = and_49_out ? and_49_out : 1'bz;  // Driver driver_122
  assign RAM_OE = and_49_out ? and_49_out : 1'bz;  // Driver driver_123
  assign driver_124_out = and_49_out ? and_49_out : 1'bz;  // Driver driver_124
  assign driver_125_out = and_49_out ? and_49_out : 1'bz;  // Driver driver_125
  assign driver_126_out = and_49_out ? and_49_out : 1'bz;  // Driver driver_126
  assign IR2RAMA = and_50_out ? and_50_out : 1'bz;  // Driver driver_127
  assign IND_CK = and_50_out ? and_50_out : 1'bz;  // Driver driver_128
  assign RAM_OE = and_50_out ? and_50_out : 1'bz;  // Driver driver_129
  assign driver_130_out = and_50_out ? and_50_out : 1'bz;  // Driver driver_130
  assign driver_131_out = and_50_out ? and_50_out : 1'bz;  // Driver driver_131
  assign INC2RAMD = and_51_out ? and_51_out : 1'bz;  // Driver driver_132
  assign RAM_WE = and_51_out ? and_51_out : 1'bz;  // Driver driver_133
  assign driver_134_out = and_51_out ? and_51_out : 1'bz;  // Driver driver_134
  assign driver_135_out = and_51_out ? and_51_out : 1'bz;  // Driver driver_135
  assign driver_136_out = and_51_out ? and_51_out : 1'bz;  // Driver driver_136
  assign IR2RAMA = and_52_out ? and_52_out : 1'bz;  // Driver driver_137
  assign RAMD2IND = and_52_out ? and_52_out : 1'bz;  // Driver driver_138
  assign RAM_OE = and_52_out ? and_52_out : 1'bz;  // Driver driver_139
  Driver driver_140 (.in(and_52_out), .en(and_52_out));  // open: out
  Driver driver_141 (.in(and_52_out), .en(and_52_out));  // open: out
  assign IR2RAMA = and_53_out ? and_53_out : 1'bz;  // Driver driver_142
  assign RAMD2IND = and_53_out ? and_53_out : 1'bz;  // Driver driver_143
  assign RAM_OE = and_53_out ? and_53_out : 1'bz;  // Driver driver_144
  assign IND_CK = and_53_out ? and_53_out : 1'bz;  // Driver driver_145
  Driver driver_146 (.in(and_53_out), .en(and_53_out));  // open: out
  assign IND2RAMA = and_54_out ? and_54_out : 1'bz;  // Driver driver_147
  assign RAMD2AC_ADD = and_54_out ? and_54_out : 1'bz;  // Driver driver_148
  assign RAM_OE = and_54_out ? and_54_out : 1'bz;  // Driver driver_149
  Driver driver_150 (.in(and_54_out), .en(and_54_out));  // open: out
  Driver driver_151 (.in(and_54_out), .en(and_54_out));  // open: out
  assign IND2RAMA = and_55_out ? and_55_out : 1'bz;  // Driver driver_152
  assign RAMD2AC_ADD = and_55_out ? and_55_out : 1'bz;  // Driver driver_153
  assign RAM_OE = and_55_out ? and_55_out : 1'bz;  // Driver driver_154
  assign AC_CK = and_55_out ? and_55_out : 1'bz;  // Driver driver_155
  assign LINK_CK = and_55_out ? and_55_out : 1'bz;  // Driver driver_156
  Counter #(.Bits(32)) u_ISZ (.en(1'b1), .C(and_56_out), .clr(1'b0), .out(ISZ_out));  // open: ovf
  and and_56 (and_56_out, ISZ, NOIND, PH02);
  and and_57 (and_57_out, ISZ, NOIND, PH03);
  and and_58 (and_58_out, ISZ, NOIND, PH04);
  and and_59 (and_59_out, ISZ, NOIND, PH05);
  and and_60 (and_60_out, ISZ, NOIND, INCZERO, PH06);
  // Probe on ISZ_out
  LED led_126 (.in(and_56_out));
  LED led_127 (.in(and_57_out));
  LED led_128 (.in(and_58_out));
  LED led_129 (.in(and_59_out));
  LED led_130 (.in(and_60_out));
  nor nor_2 (nor_2_out, AC[0], AC[1], AC[2], AC[3], AC[4], AC[5], AC[6], AC[7], AC[8], AC[9], AC[10], AC[11]);
  LED led_131 (.in(nor_2_out));
  assign IR2RAMA = and_56_out ? and_56_out : 1'bz;  // Driver driver_157
  assign RAM_OE = and_56_out ? and_56_out : 1'bz;  // Driver driver_158
  assign driver_159_out = and_56_out ? and_56_out : 1'bz;  // Driver driver_159
  assign driver_160_out = and_56_out ? and_56_out : 1'bz;  // Driver driver_160
  assign driver_161_out = and_56_out ? and_56_out : 1'bz;  // Driver driver_161
  assign IR2RAMA = and_57_out ? and_57_out : 1'bz;  // Driver driver_162
  assign RAM_OE = and_57_out ? and_57_out : 1'bz;  // Driver driver_163
  assign IND_CK = and_57_out ? and_57_out : 1'bz;  // Driver driver_164
  assign driver_165_out = and_57_out ? and_57_out : 1'bz;  // Driver driver_165
  assign driver_166_out = and_57_out ? and_57_out : 1'bz;  // Driver driver_166
  assign IR2RAMA = and_58_out ? and_58_out : 1'bz;  // Driver driver_167
  assign INC2RAMD = and_58_out ? and_58_out : 1'bz;  // Driver driver_168
  Driver driver_169 (.in(and_58_out), .en(and_58_out));  // open: out
  assign driver_170_out = and_58_out ? and_58_out : 1'bz;  // Driver driver_170
  assign driver_171_out = and_58_out ? and_58_out : 1'bz;  // Driver driver_171
  assign IR2RAMA = and_59_out ? and_59_out : 1'bz;  // Driver driver_172
  assign INC2RAMD = and_59_out ? and_59_out : 1'bz;  // Driver driver_173
  assign RAM_WE = and_59_out ? and_59_out : 1'bz;  // Driver driver_174
  assign driver_175_out = and_59_out ? and_59_out : 1'bz;  // Driver driver_175
  assign driver_176_out = and_59_out ? and_59_out : 1'bz;  // Driver driver_176
  assign PC_CK = and_60_out ? and_60_out : 1'bz;  // Driver driver_177
  assign driver_178_out = and_60_out ? and_60_out : 1'bz;  // Driver driver_178
  assign driver_179_out = and_60_out ? and_60_out : 1'bz;  // Driver driver_179
  assign driver_180_out = and_60_out ? and_60_out : 1'bz;  // Driver driver_180
  assign driver_181_out = and_60_out ? and_60_out : 1'bz;  // Driver driver_181
  and and_61 (and_61_out, nor_2_out, OPR_SZA);
  and and_62 (and_62_out, AC[11], OPR_SMA);
  and and_63 (and_63_out, OPR_SNL, LINK);
  LED led_132 (.in(and_61_out));
  LED led_133 (.in(and_62_out));
  LED led_134 (.in(and_63_out));
  or or_13 (or_13_out, and_61_out, and_62_out, and_63_out);
  Counter #(.Bits(32)) ISZ_i (.en(1'b1), .C(and_64_out), .clr(1'b0), .out(ISZ_i_out));  // open: ovf
  and and_64 (and_64_out, ISZ, IND, PH02);
  and and_65 (and_65_out, ISZ, IND, PH03);
  and and_66 (and_66_out, ISZ, IND, PH04);
  and and_67 (and_67_out, ISZ, IND, PH05);
  and and_68 (and_68_out, ISZ, IND, INCZERO, PH06);
  LED led_135 (.in(or_13_out));
  // Probe on ISZ_i_out
  LED led_136 (.in(and_64_out));
  LED led_137 (.in(and_65_out));
  LED led_138 (.in(and_66_out));
  LED led_139 (.in(and_67_out));
  LED led_140 (.in(and_68_out));
  xor xor_4 (SKIP, or_13_out, OPR_TSTINV);
  LED led_141 (.in(SKIP));
  assign IR2RAMA = and_64_out ? and_64_out : 1'bz;  // Driver driver_182
  assign RAMD2IND = and_64_out ? and_64_out : 1'bz;  // Driver driver_183
  assign RAM_OE = and_64_out ? and_64_out : 1'bz;  // Driver driver_184
  Driver driver_185 (.in(and_64_out), .en(and_64_out));  // open: out
  Driver driver_186 (.in(and_64_out), .en(and_64_out));  // open: out
  assign IR2RAMA = and_65_out ? and_65_out : 1'bz;  // Driver driver_187
  assign RAMD2IND = and_65_out ? and_65_out : 1'bz;  // Driver driver_188
  assign RAM_OE = and_65_out ? and_65_out : 1'bz;  // Driver driver_189
  assign IND_CK = and_65_out ? and_65_out : 1'bz;  // Driver driver_190
  assign driver_191_out = and_65_out ? and_65_out : 1'bz;  // Driver driver_191
  Driver driver_192 (.in(and_66_out), .en(and_66_out));  // open: out
  Driver driver_193 (.in(and_66_out), .en(and_66_out));  // open: out
  Driver driver_194 (.in(and_66_out), .en(and_66_out));  // open: out
  Driver driver_195 (.in(and_66_out), .en(and_66_out));  // open: out
  Driver driver_196 (.in(and_66_out), .en(and_66_out));  // open: out
  Driver driver_197 (.in(and_67_out), .en(and_67_out));  // open: out
  Driver driver_198 (.in(and_67_out), .en(and_67_out));  // open: out
  Driver driver_199 (.in(and_67_out), .en(and_67_out));  // open: out
  Driver driver_200 (.in(and_67_out), .en(and_67_out));  // open: out
  assign driver_201_out = and_67_out ? and_67_out : 1'bz;  // Driver driver_201
  Driver driver_202 (.in(and_68_out), .en(and_68_out));  // open: out
  Driver driver_203 (.in(and_68_out), .en(and_68_out));  // open: out
  assign driver_204_out = and_68_out ? and_68_out : 1'bz;  // Driver driver_204
  assign driver_205_out = and_68_out ? and_68_out : 1'bz;  // Driver driver_205
  assign driver_206_out = and_68_out ? and_68_out : 1'bz;  // Driver driver_206
  Counter #(.Bits(32)) ISZ_i_auto (.en(1'b1), .C(and_69_out), .clr(1'b0), .out(ISZ_i_auto_out));  // open: ovf
  and and_69 (and_69_out, ISZ, AUTOIND, PH02);
  and and_70 (and_70_out, ISZ, AUTOIND, PH03);
  and and_71 (and_71_out, ISZ, AUTOIND, PH04);
  // Probe on ISZ_i_auto_out
  assign IR2RAMA = and_69_out ? and_69_out : 1'bz;  // Driver driver_207
  LED led_142 (.in(and_69_out));
  assign RAM_OE = and_69_out ? and_69_out : 1'bz;  // Driver driver_208
  assign driver_209_out = and_69_out ? and_69_out : 1'bz;  // Driver driver_209
  assign driver_210_out = and_69_out ? and_69_out : 1'bz;  // Driver driver_210
  assign driver_211_out = and_69_out ? and_69_out : 1'bz;  // Driver driver_211
  assign IR2RAMA = and_70_out ? and_70_out : 1'bz;  // Driver driver_212
  LED led_143 (.in(and_70_out));
  assign IND_CK = and_70_out ? and_70_out : 1'bz;  // Driver driver_213
  assign RAM_OE = and_70_out ? and_70_out : 1'bz;  // Driver driver_214
  assign driver_215_out = and_70_out ? and_70_out : 1'bz;  // Driver driver_215
  assign driver_216_out = and_70_out ? and_70_out : 1'bz;  // Driver driver_216
  assign INC2RAMD = and_71_out ? and_71_out : 1'bz;  // Driver driver_217
  LED led_144 (.in(and_71_out));
  assign RAM_WE = and_71_out ? and_71_out : 1'bz;  // Driver driver_218
  assign driver_219_out = and_71_out ? and_71_out : 1'bz;  // Driver driver_219
  assign driver_220_out = and_71_out ? and_71_out : 1'bz;  // Driver driver_220
  assign driver_221_out = and_71_out ? and_71_out : 1'bz;  // Driver driver_221
  Counter #(.Bits(32)) u_DCA (.en(1'b1), .C(and_72_out), .clr(1'b0), .out(DCA_out));  // open: ovf
  and and_72 (and_72_out, DCA, NOIND, PH02);
  and and_73 (and_73_out, DCA, NOIND, PH03);
  and and_74 (and_74_out, DCA, NOIND, PH04);
  // Probe on DCA_out
  LED led_145 (.in(and_72_out));
  LED led_146 (.in(and_73_out));
  LED led_147 (.in(and_74_out));
  assign IR2RAMA = and_72_out ? and_72_out : 1'bz;  // Driver driver_222
  assign AC2RAMD = and_72_out ? and_72_out : 1'bz;  // Driver driver_223
  assign driver_224_out = and_72_out ? and_72_out : 1'bz;  // Driver driver_224
  assign driver_225_out = and_72_out ? and_72_out : 1'bz;  // Driver driver_225
  assign driver_226_out = and_72_out ? and_72_out : 1'bz;  // Driver driver_226
  assign IR2RAMA = and_73_out ? and_73_out : 1'bz;  // Driver driver_227
  assign AC2RAMD = and_73_out ? and_73_out : 1'bz;  // Driver driver_228
  assign RAM_WE = and_73_out ? and_73_out : 1'bz;  // Driver driver_229
  assign CLA = and_73_out ? and_73_out : 1'bz;  // Driver driver_230
  assign driver_231_out = and_73_out ? and_73_out : 1'bz;  // Driver driver_231
  assign CLAx = and_74_out ? and_74_out : 1'bz;  // Driver driver_232
  assign ROT2AC = and_74_out ? and_74_out : 1'bz;  // Driver driver_233
  assign AC_CK = and_74_out ? and_74_out : 1'bz;  // Driver driver_234
  assign driver_235_out = and_74_out ? and_74_out : 1'bz;  // Driver driver_235
  assign driver_236_out = and_74_out ? and_74_out : 1'bz;  // Driver driver_236
  Counter #(.Bits(32)) DCA_i (.en(1'b1), .C(and_75_out), .clr(1'b0), .out(DCA_i_out));  // open: ovf
  and and_75 (and_75_out, DCA, IND, PH02);
  and and_76 (and_76_out, DCA, IND, PH03);
  // Probe on DCA_i_out
  LED led_148 (.in(and_75_out));
  LED led_149 (.in(and_76_out));
  assign IR2RAMA = and_75_out ? and_75_out : 1'bz;  // Driver driver_237
  assign RAMD2IND = and_75_out ? and_75_out : 1'bz;  // Driver driver_238
  assign RAM_OE = and_75_out ? and_75_out : 1'bz;  // Driver driver_239
  assign driver_240_out = and_75_out ? and_75_out : 1'bz;  // Driver driver_240
  assign driver_241_out = and_75_out ? and_75_out : 1'bz;  // Driver driver_241
  assign IR2RAMA = and_76_out ? and_76_out : 1'bz;  // Driver driver_242
  assign RAMD2IND = and_76_out ? and_76_out : 1'bz;  // Driver driver_243
  assign RAM_OE = and_76_out ? and_76_out : 1'bz;  // Driver driver_244
  assign IND_CK = and_76_out ? and_76_out : 1'bz;  // Driver driver_245
  assign driver_246_out = and_76_out ? and_76_out : 1'bz;  // Driver driver_246
  Counter #(.Bits(32)) DCA_i_auto (.en(1'b1), .C(and_77_out), .clr(1'b0), .out(DCA_i_auto_out));  // open: ovf
  and and_77 (and_77_out, DCA, AUTOIND, PH02);
  and and_78 (and_78_out, DCA, AUTOIND, PH03);
  and and_79 (and_79_out, DCA, AUTOIND, PH04);
  and and_80 (and_80_out, DCA, IND, PH05);
  and and_81 (and_81_out, DCA, IND, PH06);
  // Probe on DCA_i_auto_out
  LED led_150 (.in(and_77_out));
  LED led_151 (.in(and_78_out));
  LED led_152 (.in(and_79_out));
  LED led_153 (.in(and_80_out));
  LED led_154 (.in(and_81_out));
  assign IR2RAMA = and_77_out ? and_77_out : 1'bz;  // Driver driver_247
  assign RAM_OE = and_77_out ? and_77_out : 1'bz;  // Driver driver_248
  assign driver_249_out = and_77_out ? and_77_out : 1'bz;  // Driver driver_249
  assign driver_250_out = and_77_out ? and_77_out : 1'bz;  // Driver driver_250
  assign driver_251_out = and_77_out ? and_77_out : 1'bz;  // Driver driver_251
  assign IR2RAMA = and_78_out ? and_78_out : 1'bz;  // Driver driver_252
  assign IND_CK = and_78_out ? and_78_out : 1'bz;  // Driver driver_253
  assign RAM_OE = and_78_out ? and_78_out : 1'bz;  // Driver driver_254
  assign driver_255_out = and_78_out ? and_78_out : 1'bz;  // Driver driver_255
  assign driver_256_out = and_78_out ? and_78_out : 1'bz;  // Driver driver_256
  assign INC2RAMD = and_79_out ? and_79_out : 1'bz;  // Driver driver_257
  assign RAM_WE = and_79_out ? and_79_out : 1'bz;  // Driver driver_258
  assign driver_259_out = and_79_out ? and_79_out : 1'bz;  // Driver driver_259
  assign driver_260_out = and_79_out ? and_79_out : 1'bz;  // Driver driver_260
  assign driver_261_out = and_79_out ? and_79_out : 1'bz;  // Driver driver_261
  assign IR2RAMA = and_80_out ? and_80_out : 1'bz;  // Driver driver_262
  assign RAMD2IND = and_80_out ? and_80_out : 1'bz;  // Driver driver_263
  assign RAM_OE = and_80_out ? and_80_out : 1'bz;  // Driver driver_264
  assign driver_265_out = and_80_out ? and_80_out : 1'bz;  // Driver driver_265
  assign driver_266_out = and_80_out ? and_80_out : 1'bz;  // Driver driver_266
  assign IR2RAMA = and_81_out ? and_81_out : 1'bz;  // Driver driver_267
  assign RAMD2IND = and_81_out ? and_81_out : 1'bz;  // Driver driver_268
  assign RAM_OE = and_81_out ? and_81_out : 1'bz;  // Driver driver_269
  assign IND_CK = and_81_out ? and_81_out : 1'bz;  // Driver driver_270
  assign driver_271_out = and_81_out ? and_81_out : 1'bz;  // Driver driver_271
  and and_82 (and_82_out, JMS, NOIND, PH05);
  and and_83 (and_83_out, JMS, NOIND, PH06);
  Counter #(.Bits(32)) u_JMS (.en(1'b1), .C(and_84_out), .clr(1'b0), .out(JMS_out));  // open: ovf
  and and_84 (and_84_out, JMS, NOIND, PH02);
  LED led_155 (.in(and_84_out));
  and and_85 (and_85_out, JMS, NOIND, PH03);
  LED led_156 (.in(and_85_out));
  and and_86 (and_86_out, JMS, NOIND, PH04);
  LED led_157 (.in(and_86_out));
  LED led_158 (.in(and_82_out));
  LED led_159 (.in(and_83_out));
  // Probe on JMS_out
  assign PC2RAMD = and_84_out ? and_84_out : 1'bz;  // Driver driver_272
  assign IR2RAMA = and_84_out ? and_84_out : 1'bz;  // Driver driver_273
  assign driver_274_out = and_84_out ? and_84_out : 1'bz;  // Driver driver_274
  assign driver_275_out = and_84_out ? and_84_out : 1'bz;  // Driver driver_275
  assign driver_276_out = and_84_out ? and_84_out : 1'bz;  // Driver driver_276
  assign PC2RAMD = and_85_out ? and_85_out : 1'bz;  // Driver driver_277
  assign IR2RAMA = and_85_out ? and_85_out : 1'bz;  // Driver driver_278
  assign RAM_WE = and_85_out ? and_85_out : 1'bz;  // Driver driver_279
  assign IR2PC = and_85_out ? and_85_out : 1'bz;  // Driver driver_280
  assign driver_281_out = and_85_out ? and_85_out : 1'bz;  // Driver driver_281
  assign IR2PC = and_86_out ? and_86_out : 1'bz;  // Driver driver_282
  assign PC_LD = and_86_out ? and_86_out : 1'bz;  // Driver driver_283
  assign PC_CK = and_86_out ? and_86_out : 1'bz;  // Driver driver_284
  assign driver_285_out = and_86_out ? and_86_out : 1'bz;  // Driver driver_285
  assign driver_286_out = and_86_out ? and_86_out : 1'bz;  // Driver driver_286
  assign driver_287_out = and_82_out ? and_82_out : 1'bz;  // Driver driver_287
  assign driver_288_out = and_82_out ? and_82_out : 1'bz;  // Driver driver_288
  assign driver_289_out = and_82_out ? and_82_out : 1'bz;  // Driver driver_289
  assign driver_290_out = and_82_out ? and_82_out : 1'bz;  // Driver driver_290
  assign driver_291_out = and_82_out ? and_82_out : 1'bz;  // Driver driver_291
  assign PC_CK = and_83_out ? and_83_out : 1'bz;  // Driver driver_292
  assign driver_293_out = and_83_out ? and_83_out : 1'bz;  // Driver driver_293
  assign driver_294_out = and_83_out ? and_83_out : 1'bz;  // Driver driver_294
  assign driver_295_out = and_83_out ? and_83_out : 1'bz;  // Driver driver_295
  Driver driver_296 (.in(and_83_out), .en(and_83_out));  // open: out
  Counter #(.Bits(32)) JMS_i (.en(1'b1), .C(and_87_out), .clr(1'b0), .out(JMS_i_out));  // open: ovf
  and and_87 (and_87_out, JMS, IND, PH02);
  and and_88 (and_88_out, JMS, IND, PH03);
  and and_89 (and_89_out, JMS, IND, PH04);
  and and_90 (and_90_out, JMS, IND, PH05);
  and and_91 (and_91_out, JMS, IND, PH06);
  and and_92 (and_92_out, JMS, IND, PH07);
  and and_93 (and_93_out, JMS, IND, PH08);
  // Probe on JMS_i_out
  LED led_160 (.in(and_87_out));
  LED led_161 (.in(and_88_out));
  LED led_162 (.in(and_89_out));
  LED led_163 (.in(and_90_out));
  LED led_164 (.in(and_91_out));
  LED led_165 (.in(and_92_out));
  LED led_166 (.in(and_93_out));
  assign IR2RAMA = and_87_out ? and_87_out : 1'bz;  // Driver driver_297
  assign RAMD2IND = and_87_out ? and_87_out : 1'bz;  // Driver driver_298
  assign RAM_OE = and_87_out ? and_87_out : 1'bz;  // Driver driver_299
  assign driver_300_out = and_87_out ? and_87_out : 1'bz;  // Driver driver_300
  assign driver_301_out = and_87_out ? and_87_out : 1'bz;  // Driver driver_301
  assign IR2RAMA = and_88_out ? and_88_out : 1'bz;  // Driver driver_302
  assign RAMD2IND = and_88_out ? and_88_out : 1'bz;  // Driver driver_303
  assign RAM_OE = and_88_out ? and_88_out : 1'bz;  // Driver driver_304
  assign IND_CK = and_88_out ? and_88_out : 1'bz;  // Driver driver_305
  assign driver_306_out = and_88_out ? and_88_out : 1'bz;  // Driver driver_306
  assign IND2RAMA = and_89_out ? and_89_out : 1'bz;  // Driver driver_307
  assign PC2RAMD = and_89_out ? and_89_out : 1'bz;  // Driver driver_308
  Driver driver_309 (.in(and_89_out), .en(and_89_out));  // open: out
  assign driver_310_out = and_89_out ? and_89_out : 1'bz;  // Driver driver_310
  assign driver_311_out = and_89_out ? and_89_out : 1'bz;  // Driver driver_311
  assign IND2RAMA = and_90_out ? and_90_out : 1'bz;  // Driver driver_312
  assign PC2RAMD = and_90_out ? and_90_out : 1'bz;  // Driver driver_313
  assign RAM_WE = and_90_out ? and_90_out : 1'bz;  // Driver driver_314
  assign PC_LD = and_90_out ? and_90_out : 1'bz;  // Driver driver_315
  assign IND2PC = and_90_out ? and_90_out : 1'bz;  // Driver driver_316
  assign IND2PC = and_91_out ? and_91_out : 1'bz;  // Driver driver_317
  assign PC_LD = and_91_out ? and_91_out : 1'bz;  // Driver driver_318
  assign PC_CK = and_91_out ? and_91_out : 1'bz;  // Driver driver_319
  Driver driver_320 (.in(and_91_out), .en(and_91_out));  // open: out
  assign driver_321_out = and_91_out ? and_91_out : 1'bz;  // Driver driver_321
  Driver driver_322 (.in(and_92_out), .en(and_92_out));  // open: out
  Driver driver_323 (.in(and_92_out), .en(and_92_out));  // open: out
  assign driver_324_out = and_92_out ? and_92_out : 1'bz;  // Driver driver_324
  assign driver_325_out = and_92_out ? and_92_out : 1'bz;  // Driver driver_325
  assign driver_326_out = and_92_out ? and_92_out : 1'bz;  // Driver driver_326
  assign PC_CK = and_93_out ? and_93_out : 1'bz;  // Driver driver_327
  assign driver_328_out = and_93_out ? and_93_out : 1'bz;  // Driver driver_328
  assign driver_329_out = and_93_out ? and_93_out : 1'bz;  // Driver driver_329
  assign driver_330_out = and_93_out ? and_93_out : 1'bz;  // Driver driver_330
  Driver driver_331 (.in(and_93_out), .en(and_93_out));  // open: out
  Counter #(.Bits(32)) JMS_i_auto (.en(1'b1), .C(and_94_out), .clr(1'b0), .out(JMS_i_auto_out));  // open: ovf
  and and_94 (and_94_out, JMS, AUTOIND, PH02);
  and and_95 (and_95_out, JMS, AUTOIND, PH03);
  and and_96 (and_96_out, JMS, AUTOIND, PH04);
  // Probe on JMS_i_auto_out
  assign IR2RAMA = and_94_out ? and_94_out : 1'bz;  // Driver driver_332
  LED led_167 (.in(and_94_out));
  assign RAM_OE = and_94_out ? and_94_out : 1'bz;  // Driver driver_333
  assign driver_334_out = and_94_out ? and_94_out : 1'bz;  // Driver driver_334
  assign driver_335_out = and_94_out ? and_94_out : 1'bz;  // Driver driver_335
  assign driver_336_out = and_94_out ? and_94_out : 1'bz;  // Driver driver_336
  assign IR2RAMA = and_95_out ? and_95_out : 1'bz;  // Driver driver_337
  LED led_168 (.in(and_95_out));
  assign IND_CK = and_95_out ? and_95_out : 1'bz;  // Driver driver_338
  assign RAM_OE = and_95_out ? and_95_out : 1'bz;  // Driver driver_339
  assign driver_340_out = and_95_out ? and_95_out : 1'bz;  // Driver driver_340
  assign driver_341_out = and_95_out ? and_95_out : 1'bz;  // Driver driver_341
  assign INC2RAMD = and_96_out ? and_96_out : 1'bz;  // Driver driver_342
  LED led_169 (.in(and_96_out));
  assign RAM_WE = and_96_out ? and_96_out : 1'bz;  // Driver driver_343
  assign driver_344_out = and_96_out ? and_96_out : 1'bz;  // Driver driver_344
  assign driver_345_out = and_96_out ? and_96_out : 1'bz;  // Driver driver_345
  assign driver_346_out = and_96_out ? and_96_out : 1'bz;  // Driver driver_346
  Counter #(.Bits(32)) u_JMP (.en(1'b1), .C(and_97_out), .clr(1'b0), .out(JMP_out));  // open: ovf
  and and_97 (and_97_out, JMP, NOIND, PH02);
  LED led_170 (.in(and_97_out));
  and and_98 (and_98_out, JMP, NOIND, PH03);
  LED led_171 (.in(and_98_out));
  // Probe on JMP_out
  assign IR2PC = and_97_out ? and_97_out : 1'bz;  // Driver driver_347
  assign driver_348_out = and_97_out ? and_97_out : 1'bz;  // Driver driver_348
  assign driver_349_out = and_97_out ? and_97_out : 1'bz;  // Driver driver_349
  assign driver_350_out = and_97_out ? and_97_out : 1'bz;  // Driver driver_350
  assign driver_351_out = and_97_out ? and_97_out : 1'bz;  // Driver driver_351
  assign IR2PC = and_98_out ? and_98_out : 1'bz;  // Driver driver_352
  assign PC_LD = and_98_out ? and_98_out : 1'bz;  // Driver driver_353
  assign PC_CK = and_98_out ? and_98_out : 1'bz;  // Driver driver_354
  assign driver_355_out = and_98_out ? and_98_out : 1'bz;  // Driver driver_355
  assign driver_356_out = and_98_out ? and_98_out : 1'bz;  // Driver driver_356
  Counter #(.Bits(32)) JMP_i (.en(1'b1), .C(and_99_out), .clr(1'b0), .out(JMP_i_out));  // open: ovf
  and and_99 (and_99_out, JMP, IND, PH02);
  and and_100 (and_100_out, JMP, IND, PH03);
  // Probe on JMP_i_out
  LED led_172 (.in(and_99_out));
  LED led_173 (.in(and_100_out));
  assign IR2RAMA = and_99_out ? and_99_out : 1'bz;  // Driver driver_357
  assign RAMD2PC = and_99_out ? and_99_out : 1'bz;  // Driver driver_358
  assign RAM_OE = and_99_out ? and_99_out : 1'bz;  // Driver driver_359
  assign driver_360_out = and_99_out ? and_99_out : 1'bz;  // Driver driver_360
  assign driver_361_out = and_99_out ? and_99_out : 1'bz;  // Driver driver_361
  assign IR2RAMA = and_100_out ? and_100_out : 1'bz;  // Driver driver_362
  assign RAMD2PC = and_100_out ? and_100_out : 1'bz;  // Driver driver_363
  assign RAM_OE = and_100_out ? and_100_out : 1'bz;  // Driver driver_364
  assign PC_LD = and_100_out ? and_100_out : 1'bz;  // Driver driver_365
  assign PC_CK = and_100_out ? and_100_out : 1'bz;  // Driver driver_366
  Counter #(.Bits(32)) JMP_i_auto (.en(1'b1), .C(and_101_out), .clr(1'b0), .out(JMP_i_auto_out));  // open: ovf
  and and_101 (and_101_out, JMP, AUTOIND, PH02);
  and and_102 (and_102_out, JMP, AUTOIND, PH03);
  and and_103 (and_103_out, JMP, AUTOIND, PH04);
  and and_104 (and_104_out, JMP, AUTOIND, PH05);
  and and_105 (and_105_out, JMP, AUTOIND, PH06);
  // Probe on JMP_i_auto_out
  LED led_174 (.in(and_101_out));
  LED led_175 (.in(and_102_out));
  LED led_176 (.in(and_103_out));
  LED led_177 (.in(and_104_out));
  LED led_178 (.in(and_105_out));
  assign IR2RAMA = and_101_out ? and_101_out : 1'bz;  // Driver driver_367
  assign RAM_OE = and_101_out ? and_101_out : 1'bz;  // Driver driver_368
  assign driver_369_out = and_101_out ? and_101_out : 1'bz;  // Driver driver_369
  assign driver_370_out = and_101_out ? and_101_out : 1'bz;  // Driver driver_370
  assign driver_371_out = and_101_out ? and_101_out : 1'bz;  // Driver driver_371
  assign IR2RAMA = and_102_out ? and_102_out : 1'bz;  // Driver driver_372
  assign IND_CK = and_102_out ? and_102_out : 1'bz;  // Driver driver_373
  assign RAM_OE = and_102_out ? and_102_out : 1'bz;  // Driver driver_374
  assign driver_375_out = and_102_out ? and_102_out : 1'bz;  // Driver driver_375
  assign driver_376_out = and_102_out ? and_102_out : 1'bz;  // Driver driver_376
  assign INC2RAMD = and_103_out ? and_103_out : 1'bz;  // Driver driver_377
  assign RAM_WE = and_103_out ? and_103_out : 1'bz;  // Driver driver_378
  assign driver_379_out = and_103_out ? and_103_out : 1'bz;  // Driver driver_379
  assign driver_380_out = and_103_out ? and_103_out : 1'bz;  // Driver driver_380
  assign driver_381_out = and_103_out ? and_103_out : 1'bz;  // Driver driver_381
  assign IR2RAMA = and_104_out ? and_104_out : 1'bz;  // Driver driver_382
  assign RAMD2PC = and_104_out ? and_104_out : 1'bz;  // Driver driver_383
  assign RAM_OE = and_104_out ? and_104_out : 1'bz;  // Driver driver_384
  assign driver_385_out = and_104_out ? and_104_out : 1'bz;  // Driver driver_385
  assign driver_386_out = and_104_out ? and_104_out : 1'bz;  // Driver driver_386
  assign IR2RAMA = and_105_out ? and_105_out : 1'bz;  // Driver driver_387
  assign RAMD2PC = and_105_out ? and_105_out : 1'bz;  // Driver driver_388
  assign RAM_OE = and_105_out ? and_105_out : 1'bz;  // Driver driver_389
  assign PC_LD = and_105_out ? and_105_out : 1'bz;  // Driver driver_390
  assign PC_CK = and_105_out ? and_105_out : 1'bz;  // Driver driver_391
  Counter #(.Bits(32)) OPR_GRP1 (.en(1'b1), .C(and_106_out), .clr(1'b0), .out(OPR_GRP1_out));  // open: ovf
  and and_106 (and_106_out, OPR1, NOTNOP, PH02);
  LED led_179 (.in(and_106_out));
  and and_107 (and_107_out, OPR1, 1'b1, PH03);
  LED led_180 (.in(and_107_out));
  // Probe on OPR_GRP1_out
  assign ROT2AC = and_106_out ? and_106_out : 1'bz;  // Driver driver_392
  Driver driver_393 (.in(and_106_out), .en(and_106_out));  // open: out
  Driver driver_394 (.in(and_106_out), .en(and_106_out));  // open: out
  Driver driver_395 (.in(and_106_out), .en(and_106_out));  // open: out
  Driver driver_396 (.in(and_106_out), .en(and_106_out));  // open: out
  assign AC_CK = and_107_out ? and_107_out : 1'bz;  // Driver driver_397
  assign LINK_CK = and_107_out ? and_107_out : 1'bz;  // Driver driver_398
  assign ROT2AC = and_107_out ? and_107_out : 1'bz;  // Driver driver_399
  Driver driver_400 (.in(and_107_out), .en(and_107_out));  // open: out
  Driver driver_401 (.in(and_107_out), .en(and_107_out));  // open: out
  Driver driver_402 (.in(and_107_out), .en(and_107_out));  // open: out
  Counter #(.Bits(32)) OPR_GRP2 (.en(1'b1), .C(and_108_out), .clr(1'b0), .out(OPR_GRP2_out));  // open: ovf
  and and_108 (and_108_out, OPR2, NOTNOP, PH02);
  and and_109 (and_109_out, OPR2, 1'b1, PH03);
  and and_110 (and_110_out, OPR2, SKIP, PH04);
  // Probe on OPR_GRP2_out
  LED led_181 (.in(and_108_out));
  LED led_182 (.in(and_109_out));
  LED led_183 (.in(and_110_out));
  assign ROT2AC = and_108_out ? and_108_out : 1'bz;  // Driver driver_403
  Driver driver_404 (.in(and_108_out), .en(and_108_out));  // open: out
  Driver driver_405 (.in(and_108_out), .en(and_108_out));  // open: out
  Driver driver_406 (.in(and_108_out), .en(and_108_out));  // open: out
  Driver driver_407 (.in(and_108_out), .en(and_108_out));  // open: out
  assign AC_CK = and_109_out ? and_109_out : 1'bz;  // Driver driver_408
  assign ROT2AC = and_109_out ? and_109_out : 1'bz;  // Driver driver_409
  Driver driver_410 (.in(and_109_out), .en(and_109_out));  // open: out
  Driver driver_411 (.in(and_109_out), .en(and_109_out));  // open: out
  Driver driver_412 (.in(and_109_out), .en(and_109_out));  // open: out
  assign IR_CK = and_110_out ? and_110_out : 1'bz;  // Driver driver_413
  assign PC_CK = and_110_out ? and_110_out : 1'bz;  // Driver driver_414
  Driver driver_415 (.in(and_110_out), .en(and_110_out));  // open: out
  Driver driver_416 (.in(and_110_out), .en(and_110_out));  // open: out
  Driver driver_417 (.in(and_110_out), .en(and_110_out));  // open: out

  // Other names for the same wires on the sheet: PI0[2:0] = PCIN[2:0]; PI1[2:0] = PCIN[5:3]; PI2[2:0] = PCIN[8:6];
  //   PI3[2:0] = PCIN[11:9]; RAMADDR[11:0] = {RA3, RA2, RA1, RA0}; AC0[2:0] = AC[2:0]; AC1[2:0] = AC[5:3];
  //   AC2[2:0] = AC[8:6]; AC3[2:0] = AC[11:9]; IR0[2:0] = BUS_IR[2:0]; IR1[2:0] = BUS_IR[5:3]; IR2[2:0] = BUS_IR[8:6];
  //   MP = BUS_IR[7]; IR3[2:0] = BUS_IR[11:9]; PC0[2:0] = BUS_PC[2:0]; PC1[2:0] = BUS_PC[5:3]; PC2[2:0] = BUS_PC[8:6];
  //   PC3[2:0] = BUS_PC[11:9]; DATA[11:0] = {DA3, DA2, DA1, DA0}; INDOUT[11:0] = {IND3, IND2, IND1, IND0};
  //   RD0[2:0] = RAMDATA[2:0]; RD1[2:0] = RAMDATA[5:3]; RD2[2:0] = RAMDATA[8:6]; RD3[2:0] = RAMDATA[11:9]

  // Notes on the sheet:
  //   clk: Hz: 10000
  //   IOT DECODER
  //   PH0 & PH1
  //   IR DECODER
  //   OPR DECODER
  //   PC
  //   IR
  //   AC
  //   IND
  //   RAM-A
  //   RAM-D
  //   PC-IN
  //   DATA
  //   KCF
  //   CLA
  //   AND
  //   KSF
  //   CLL
  //   TAD
  //   KCC
  //   KRS
  //   CMA
  //   CMI
  //   ISZ
  //   DCA
  //   INSTRUCTION
  //   KIE
  //   IAC
  //   JMS
  //   STATE
  //   RUN
  //   HALT
  //   AUTO
  //   PC=0200
  //   KRB
  //   ROR
  //   JMP
  //   PCIN
  //   TFL
  //   ROL
  //   x2
  //   IOT
  //   OPR
  //   TSF
  //   TCF
  //   SMA
  //   DIR
  //   START/STOP/STEP
  //   CLOCK CYCLE CONTROLLER
  //   TPC
  //   TSK
  //   SZA
  //   SNL
  //   AUTO
  //   IND
  //   AUTO CNT
  //   (DECIMAL}
  //   PCOUT
  //   TLS
  //   INV
  //   CURR
  //   PAGE
  //   OSR
  //   HLT
  //   -
  //   RAMADDR
  //   NOP
  //   contents of eeprom_1 (hex, n*v repeats v):
  //   f02,f02,f02,f02,f02,f02,f02,f02,9c,f02,f02,f02,f02,f02,f02,f02,f02,f02,f02,f02,f02,
  //   f02,f02,f02,f02,f02,f02,f02,f02,f02,f02,f02,f02,f02,f02,f02,f02,f02,f02,f02,f02,f02,
  //   f02,f02,f02,f02,f02,f02,f02,f02,f02,f02,f02,f02,f02,f02,f02,f02,f02,f02,f02,f02,f02,
  //   f02,f02,f02,f02,f02,f02,f02,f02,f02,f02,f02,f02,f02,f02,f02,f02,f02,f02,f02,f02,f02,
  //   f02,f02,f02,f02,f02,f02,f02,f02,f02,f02,f02,f02,f02,f02,f02,f02,f02,f02,f02,f02,f02,
  //   f02,f02,f02,f02,f02,f02,f02,f02,f02,f02,f02,f02,f02,f02,f02,f02,f02,f02,f02,f02,f02,
  //   f02,f02,e80,e40,28f,608,308,f28,f02,889,a84,88,c26,c21,a8b,e80,b89,8f,48,45,4c,4c,
  //   4f,20,57,4f,52,4c,44,21,0,422,f02,f02,f02,f02,f02,f02,f02,f02,f02,f02,f02,f02,f02,
  //   f02,f02,f02,f02,f02,f02,f02,f02,f02,f02,f02,f02,f02,f02,f02,f02,f02,f02,f02,f02,f02,
  //   f02,f02,f02,f02,f02,f02,f02,f02,f02,f02,f02,f02,f02,f02,f02,f02,f02,f02,f02,f02,f02,
  //   f02,f02,f02,f02,f02,f02,f02,f02,f02,f02,f02,f02,f02,f02,f02,f02,f02,f02,f02,f02,f02,
  //   f02,f02,f02,f02,f02,f02,f02,f02,f02,f02,f02,f02,f02,f02,f02,f02,f02,f02,f02,f02,f02,
  //   f02,f02,f02,f02,f02,f02,f02,f02,f02,f02,f02,f02,f02,f02,f02,f02,f02,f02,f02,f02,f02,
  //   f02,f02,f02,f02,f02,f02,f02,f02,f02,f02,f02,f02,f02,f02,f02,f02,f02,f02,f02,f02,f02,
  //   f02,f02,f02,f02,f02,f02,f02,f02,f02,f02,f02,f02,f02,f02,f02,f02,f02,f02,f02,f02,f02,
  //   f02,f02,f02,f02,f02,f02,f02,f02,f02,f02,f02,f02,f02,f02,f02,f02,f02,f02,f02,f02,f02,
  //   f02,f02,f02,f02,f02,f02,f02,f02,f02,f02,f02,f02,f02,f02,f02,f02,f02,f02,f02,f02,f02,
  //   f02,f02,f02,f02,f02,f02,f02,f02,f02,f02,f02,f02,f02,f02,f02,f02,f02,f02,f02,f02,f02,
  //   f02,f02,f02,f02,f02,f02,f02,f02,f02,f02,f02,f02,f02,f02,f02,f02,f02,f02,f02,f02,f02,
  //   f02,f02,f02,f02,f02,f02,f02,f02,f02,f02,f02,f02,f02,f02,f02,f02,f02,f02,f02,f02,f02,
  //   f02,f02,f02,f02,f02,f02,f02,f02,f02,f02,f02,f02,f02,f02,f02,f02,f02,f02,f02,f02,f02,
  //   f02,f02,f02,f02,f02,f02,f02,f02,f02,f02,f02,f02,f02,f02,f02,f02,f02,f02,f02,f02,f02,
  //   f02,f02,f02,f02,f02,f02,f02,f02,f02,f02,f02,f02,f02,f02,f02,f02,f02,f02,f02,f02,f02,
  //   f02,f02,f02,f02,f02,f02,f02,f02,f02,f02,f02,f02,f02,f02,f02,f02,f02,f02,f02,f02,f02,
  //   f02,f02,f02,f02,f02,f02,f02,f02,f02,f02,f02,f02,f02,f02,f02,f02,f02,f02,f02,f02,f02,
  //   f02,f02,f02,f02,f02,f02,f02,f02,f02,f02,f02,f02,f02,f02,f02,f02,f02,f02,f02,f02,f02,
  //   f02,f02,f02,f02,f02,f02,f02,f02,f02,f02,f02,f02,f02,f02,f02,f02,f02,f02,f02,f02,f02,
  //   f02,f02,f02,f02,f02,f02,f02,f02,f02,f02,f02,f02,f02,f02,f02,f02,f02,f02,f02,f02,f02,
  //   f02,f02,f02,f02,f02,f02,f02,f02,f02,f02,f02,f02,f02,f02,f02,f02,f02,f02,f02,f02,f02,
  //   f02,f02,f02,f02,f02,f02,f02,f02,f02,f02,f02,f02,f02,f02,f02,f02,f02,f02,f02,f02,f02,
  //   f02,f02,f02,f02,f02,f02,f02,f02,f02,f02,f02,f02,f02,f02,f02,f02,f02,f02,f02,f02,f02,
  //   f02,f02,f02,f02,f02,f02,f02,f02,f02,f02,f02,f02,f02,f02,f02,f02,f02,f02,f02,f02,f02,
  //   f02,f02,f02,f02,f02,f02,f02,f02,f02,f02,f02,f02,f02,f02,f02,f02,f02,f02,f02,f02,f02,
  //   f02,f02,f02,f02,f02,f02,f02,f02,f02,f02,f02,f02,f02,f02,f02,f02,f02,f02,f02,f02,f02,
  //   f02,f02,f02,f02,f02,f02,f02,f02,f02,f02,f02,f02,f02,f02,f02,f02,f02,f02,f02,f02,f02,
  //   f02,f02,f02,f02,f02,f02,f02,f02,f02,f02,f02,f02,f02,f02,f02,f02,f02,f02,f02,f02,f02,
  //   f02,f02,f02,f02,f02,f02,f02,f02,f02,f02,f02,f02,f02,f02,f02,f02,f02,f02,f02,f02,f02,
  //   f02,f02,f02,f02,f02,f02,f02,f02,f02,f02,f02,f02,f02,f02,f02,f02,f02,f02,f02,f02,f02,
  //   f02,f02,f02,f02,f02,f02,f02,f02,f02,f02,f02,f02,f02,f02,f02,f02,f02,f02,f02,f02,f02,
  //   f02,f02,f02,f02,f02,f02,f02,f02,f02,f02,f02,f02,f02,f02,f02,f02,f02,f02,f02,f02,f02,
  //   f02,f02,f02,f02,f02,f02,f02,f02,f02,f02,f02,f02,f02,f02,f02,f02,f02,f02,f02,f02,f02,
  //   f02,f02,f02,f02,f02,f02,f02,f02,f02,f02,f02,f02,f02,f02,f02,f02,f02,f02,f02,f02,f02,
  //   f02,f02,f02,f02,f02,f02,f02,f02,f02,f02,f02,f02,f02,f02,f02,f02,f02,f02,f02,f02,f02,
  //   f02,f02,f02,f02,f02,f02,f02,f02,f02,f02,f02,f02,f02,f02,f02,f02,f02,f02,f02,f02,f02,
  //   f02,f02,f02,f02,f02,f02,f02,f02,f02,f02,f02,f02,f02,f02,f02,f02,f02,f02,f02,f02,f02,
  //   f02,f02,f02,f02,f02,f02,f02,f02,f02,f02,f02,f02,f02,f02,f02,f02,f02,f02,f02,f02,f02,
  //   f02,f02,f02,f02,f02,f02,f02,f02,f02,f02,f02,f02,f02,f02,f02,f02,f02,f02,f02,f02,f02,
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  //   RAMDATA
  //   AND
  //   STEP1
  //   INDOUT
  //   IND
  //   STEP1
  //   IND
  //   STEP2
  //   AND
  //   STEP2
  //   iAuto 1
  //   iAuto 2
  //   iAuto 3
  //   TAD
  //   STEP1
  //   TAD
  //   STEP2
  //   CML
  //   Prepare to store
  //   return address
  //   Actually store
  //   return address
  //   Pause to accept
  //   new PC inc clk
  //   Actually increment
  //   PC
  //   Actually set
  //   PC
  //   Prepate to store 
  //   return addr
  //   to [ind]
  //   Store return addr
  //   to [ind]
  //   Prepare to set
  //   new PC
  //   Actually set
  //   new PC
  //   Prepare to set PC
  //   with new vector
endmodule
